# Fritzing sketch Double Box Parts Sketch (saved by Fritzing 0.9.2b)
breadboards: 1

parts:
  U1 = OP27 - Low Noise, Precision Op Amp [part_number=OP27]  # not connected
  C1 = Tantalum Capacitor [capacitance=100nF package="100 mil [THT, tantalum]"]
  C4 = Capacitor [package=cap-pth-small2]
  C3 = Capacitor [package=cap-pth-small]
  C3_2 = Capacitor [package=cap-pth-small]
  C3_3 = Capacitor [package=cap-pth-5mm]
  C3_4 = Capacitor [package=cap-pth-small]
  C3_5 = Capacitor [package=cap-pth-small-kit]
  C5 = Tantalum Capacitor [capacitance="1 μF" package="A 3216 [SMD, tantalum]"]
  U2 = OP27 - Low Noise, Precision Op Amp [part_number=OP27]  # not connected
  C6 = Capacitor [package=cap-pth-small2]
  C2 = Capacitor [package=cap-pth-small2]
  C7 = Capacitor [package=cap-pth-5mm]
  R2 = Resistor [tolerance=±5% resistance=220k package=THT]
  Q1 = Basic FET P-Channel [package="TO220 [THT]"]
  Q2 = Basic FET P-Channel [package="TO220 [THT]"]
  Q3 = Basic FET P-Channel [package="TO220 [THT]"]
  Q4 = Basic FET P-Channel [package="TO220 [THT]"]
  Q5 = Basic FET P-Channel [package="TO220 [THT]"]
  Q6 = Basic FET P-Channel [package="TO220 [THT]"]
  R3 = Resistor [tolerance=±5% resistance=10k package=THT]
  R4 = Resistor [tolerance=±5% resistance=10k package=THT]
  R5 = Resistor [tolerance=±5% resistance=10k package=THT]
  R8 = Resistor [tolerance=±5% resistance=10k package=THT]
  R1 = Resistor [tolerance=±20% resistance=220k package="0603 [SMD]"]
  R9 = Resistor [tolerance=±5% resistance=10k package=THT]
  R10 = Resistor [tolerance=±5% resistance=10k package=THT]
  LED1 = RGB LED - (4 legs) [package="5 mm [THT]"]
  TRS1 = Audio Jack (TRS) 3.5mm [package="PG203J [THT]"]
  Part1 = Arduino Uno (Rev3)
  LED2 = RGB LED - (4 legs) [package="5 mm [THT]"]

nets:
  N1: C1.-, C2.1, TRS1.Ring
  N2: C4.1, C6.1, Q1.source, Q2.source, Q3.source, Q5.gate, Q6.gate, R8.Pin_0, R9.Pin_0, R10.Pin_0
  N3: C3.1, C3_2.1, C3_3.1, C3_4.1, C3_5.1, R1.Pin_0
  N4: C3.2, C3_2.2, C3_3.2, C3_4.2, C3_5.2
  N5: C5.-, TRS1.Tip
  N6: C6.2, Q4.gate, R3.Pin_1, R4.Pin_0
  N7: C7.1, R2.Pin_0
  N8: Q1.gate, Part1.D7
  N9: Q1.drain, R10.Pin_1, LED2.blue_cathode
  N10: Q2.gate, Part1.D6_PWM
  N11: Q2.drain, R8.Pin_1, LED2.green_cathode
  N12: Q3.gate, Part1.D8
  N13: Q3.drain, R9.Pin_1, LED2.common_anode
  N14: Q4.drain, R4.Pin_1, LED1.green_cathode
  N15: Q4.source, Part1.D10_PWM/SS
  N16: Q5.drain, R5.Pin_0, LED1.blue_cathode
  N17: Q5.source, Part1.D11_PWM/MOSI
  N18: Q6.drain, R3.Pin_0, LED1.common_anode
  N19: Q6.source, Part1.D9_PWM
  N20: LED1.red_cathode, TRS1.Sleeve, Part1.VIN
  N21: Part1.GND, LED2.red_cathode

notes:
  C2: 100 nf
